// Digital circuit 2 bit multiplier v2.dig as structural Verilog
module _2_bit_multiplier_v2 (
  input  [1:0] A,
  input  [1:0] B,
  output [3:0] Output
);

  wire and_2_out, and_3_out, and_4_out, and_5_out;

  and and_1 (Output[0], B[0], A[0]);
  and and_2 (and_2_out, B[0], A[1]);
  and and_3 (and_3_out, B[1], A[0]);
  and and_4 (and_4_out, B[1], A[1]);
  xor xor_1 (Output[1], and_2_out, and_3_out);
  and and_5 (and_5_out, and_2_out, and_3_out);
  xor xor_2 (Output[2], and_5_out, and_4_out);
  and and_6 (Output[3], and_5_out, and_4_out);
endmodule
