// Digital circuit Adder v1.dig as structural Verilog
module Adder_v1 (
  input  A_0,
  input  B_0,
  input  C_in0,
  output Sum_0,
  output C_out0
);

  wire and_1_out, and_2_out, xor_1_out;

  xor xor_1 (xor_1_out, A_0, B_0);
  and and_1 (and_1_out, A_0, B_0);
  xor xor_2 (Sum_0, xor_1_out, C_in0);
  and and_2 (and_2_out, xor_1_out, C_in0);
  or or_1 (C_out0, and_2_out, and_1_out);
endmodule
